// Logisim project alu8_wrong.circ as structural Verilog: 1 circuit, main circuit ALU8
module ALU8 (
  input  [7:0] A,
  input  [7:0] B,
  input  [2:0] OP,
  output [7:0] Y,
  output Z,
  output C
);

  wire ADD_C, SUB_B, SUB_NB;
  wire [7:0] ADD_S, AND_V, NOT_V, OR_V, SHL_V, SHR_V, SUB_D, XOR_V;

  Adder #(.width(8)) adder_1 (.a(A), .b(B), .out(ADD_S), .cin(1'b0), .cout(ADD_C));
  Subtractor #(.width(8)) subtractor_1 (.a(A), .b(B), .out(SUB_D), .bin(1'b0), .bout(SUB_B));
  assign AND_V = A & B;  // AND_Gate and_1, 8 bits wide
  assign OR_V = A | B;  // OR_Gate or_1, 8 bits wide
  assign XOR_V = A | B;  // OR_Gate or_2, 8 bits wide
  assign NOT_V = ~A;  // NOT_Gate not_1, 8 bits wide
  Shifter #(.width(8), .shift("ll")) shifter_1 (.in(A), .\dist (3'b001), .out(SHL_V));
  Shifter #(.width(8), .shift("lr")) shifter_2 (.in(A), .\dist (3'b001), .out(SHR_V));
  not not_2 (SUB_NB, SUB_B);
  Multiplexer #(.select(3), .width(8)) multiplexer_1 (
    .in0(ADD_S), .in1(SUB_D), .in2(AND_V), .in3(OR_V), .in4(XOR_V), .in5(NOT_V), .in6(SHL_V), .in7(SHR_V),
    .out(Y), .sel(OP));
  Multiplexer #(.select(3), .width(1)) multiplexer_2 (
    .in0(ADD_C), .in1(SUB_NB), .in2(1'b0), .in3(1'b0), .in4(1'b0), .in5(1'b0), .in6(A[7]), .in7(A[0]),
    .out(C), .sel(OP));
  nor nor_1 (Z, Y[0], Y[1], Y[2], Y[3], Y[4], Y[5], Y[6], Y[7]);

  // Other names for the same wires on the sheet: YB0 = Y[0]; YB1 = Y[1]; YB2 = Y[2]; YB3 = Y[3]; YB4 = Y[4];
  //   YB5 = Y[5]; YB6 = Y[6]; YB7 = Y[7]
endmodule
