// Logisim project cpu8.circ as structural Verilog: 1 circuit, main circuit CPU8
module CPU8 (
  input  CLK,
  input  RESET,
  input  EN,
  input  [7:0] INSTR,
  output [3:0] PC,
  output [7:0] ACC,
  output [7:0] IR,
  output [1:0] PHASE,
  output Z,
  output C,
  output HALTED,
  output ERROR
);

  wire S9, S10, S11, S12, S13, S14, S15, S16, S17, S18, S19, S20, S21, S22, S32, S33, S34, S49, S50, S51,
       S52, S53, S54, S55, S56, S57, S60, S62, S63, S69, S73, S79, S80, S81, S83, S84, S85, S86, S87, S88,
       S90, S94, S95, S96, S97, S98, S99, S100;
  wire [3:0] S3, S4, S67, S68, S70, S91;
  wire [7:0] S25, S28, S29, S30, S31, S36, S72, S74, S77, S92, S93;

  Decoder #(.select(4)) decoder_1 (
    .out0(S15), .out1(S16), .out2(S11), .out3(S12), .out4(S13), .out5(S14), .out6(S18), .out15(S19),
    .sel(S3), .en(1'b1));  // open: out7, out8, out9, out10, out11, out12, out13, out14
  Register #(.width(1)) register_1 (.D(S94), .en(S90), .clk(CLK), .Q(PHASE[0]), .clr(1'b0));
  assign S30 = ACC & S25;  // AND_Gate and_1, 8 bits wide
  Adder #(.width(4)) adder_1 (.a(PC), .b(4'b0001), .out(S67));  // open: cin, cout
  or or_1 (S20, S15, S16, S17, S18, S19);
  and and_2 (S80, S52, S53);
  Multiplexer #(.select(1), .width(4)) multiplexer_1 (.in0(S67), .in1(S4), .out(S68), .sel(S57));
  Multiplexer #(.select(1), .width(1)) multiplexer_2 (.in0(Z), .in1(S79), .out(S81), .sel(S80));
  Multiplexer #(.select(1), .width(1)) multiplexer_3 (.in0(S49), .in1(S50), .out(S79), .sel(S16));
  Multiplexer #(.select(1), .width(1)) multiplexer_4 (.in0(S56), .in1(1'b0), .out(S94), .sel(RESET));
  Register #(.width(1)) register_2 (.D(S95), .en(S90), .clk(CLK), .Q(PHASE[1]), .clr(1'b0));
  assign S31 = ACC | S25;  // OR_Gate or_2, 8 bits wide
  not not_1 (S54, S20);
  and and_3 (S85, S52, S55);
  Multiplexer #(.select(1), .width(4)) multiplexer_5 (.in0(PC), .in1(S68), .out(S70), .sel(S69));
  Multiplexer #(.select(1), .width(1)) multiplexer_6 (.in0(S81), .in1(1'b0), .out(S96), .sel(RESET));
  Multiplexer #(.select(1), .width(1)) multiplexer_7 (.in0(S51), .in1(1'b0), .out(S83), .sel(S16));
  Multiplexer #(.select(1), .width(1)) multiplexer_8 (.in0(S100), .in1(1'b0), .out(S95), .sel(RESET));
  Register #(.width(1)) register_3 (.D(S96), .en(S90), .clk(CLK), .Q(Z), .clr(1'b0));
  not not_2 (S34, S33);
  not not_3 (S10, PHASE[0]);
  or or_3 (S60, HALTED, ERROR);
  and and_4 (S87, S52, S54);
  Multiplexer #(.select(1), .width(4)) multiplexer_9 (.in0(S70), .in1(4'b0000), .out(S91), .sel(RESET));
  Multiplexer #(.select(1), .width(1)) multiplexer_10 (.in0(C), .in1(S83), .out(S84), .sel(S80));
  Register #(.width(1)) register_4 (.D(S97), .en(S90), .clk(CLK), .Q(C), .clr(1'b0));
  Multiplexer #(.select(2), .width(8)) multiplexer_11 (
    .in0(S28), .in1(S29), .in2(S30), .in3(S31), .out(S36), .sel({S22, S21}));
  not not_4 (S9, PHASE[1]);
  not not_5 (S62, S60);
  and and_5 (S57, S52, S18);
  Multiplexer #(.select(1), .width(8)) multiplexer_12 (.in0(S36), .in1(S25), .out(S72), .sel(S16));
  Multiplexer #(.select(1), .width(1)) multiplexer_13 (.in0(S84), .in1(1'b0), .out(S97), .sel(RESET));
  Register #(.width(1)) register_5 (.D(S98), .en(S90), .clk(CLK), .Q(HALTED), .clr(1'b0));
  Multiplexer #(.select(2), .width(1)) multiplexer_14 (
    .in0(S32), .in1(S34), .in2(1'b0), .in3(1'b0), .out(S51), .sel({S22, S21}));
  and and_6 (S56, S9, S10);
  and and_7 (S63, EN, S62);
  or or_4 (S69, S56, S57);
  Multiplexer #(.select(1), .width(8)) multiplexer_15 (.in0(ACC), .in1(S72), .out(S74), .sel(S73));
  Multiplexer #(.select(1), .width(1)) multiplexer_16 (.in0(HALTED), .in1(1'b1), .out(S86), .sel(S85));
  Register #(.width(4)) register_6 (.D(S91), .en(S90), .clk(CLK), .Q(PC), .clr(1'b0));
  Register #(.width(1)) register_7 (.D(S99), .en(S90), .clk(CLK), .Q(ERROR), .clr(1'b0));
  nor nor_1 (S49, S36[0], S36[1], S36[2], S36[3], S36[4], S36[5], S36[6], S36[7]);
  and and_8 (S100, S9, PHASE[0]);
  or or_5 (S90, S63, RESET);
  or or_6 (S55, S19, S54);
  Multiplexer #(.select(1), .width(8)) multiplexer_17 (.in0(S74), .in1({8{1'b0}}), .out(S92), .sel(RESET));
  Multiplexer #(.select(1), .width(1)) multiplexer_18 (.in0(S86), .in1(1'b0), .out(S98), .sel(RESET));
  BitSelector #(.width(8), .group(4)) bitselector_1 (.in(IR), .out(S4), .sel(1'b0));
  Register #(.width(8)) register_8 (.D(S92), .en(S90), .clk(CLK), .Q(ACC), .clr(1'b0));
  Adder #(.width(8)) adder_2 (.a(ACC), .b(S25), .out(S28), .cin(1'b0), .cout(S32));
  assign S25 = {{4{1'b0}}, S4};  // Bit_Extender bit_extender_1
  and and_9 (S52, PHASE[1], S10);
  or or_7 (S53, S16, S17);
  or or_8 (S21, S12, S14);
  Multiplexer #(.select(1), .width(8)) multiplexer_19 (.in0(IR), .in1(INSTR), .out(S77), .sel(S56));
  Multiplexer #(.select(1), .width(1)) multiplexer_20 (.in0(ERROR), .in1(1'b1), .out(S88), .sel(S87));
  BitSelector #(.width(8), .group(4)) bitselector_2 (.in(IR), .out(S3), .sel(1'b1));
  Register #(.width(8)) register_9 (.D(S93), .en(S90), .clk(CLK), .Q(IR), .clr(1'b0));
  Subtractor #(.width(8)) subtractor_1 (.a(ACC), .b(S25), .out(S29), .bin(1'b0), .bout(S33));
  nor nor_2 (S50, S4[0], S4[1], S4[2], S4[3]);
  or or_9 (S17, S11, S12, S13, S14);
  and and_10 (S73, S52, S53);
  or or_10 (S22, S13, S14);
  Multiplexer #(.select(1), .width(8)) multiplexer_21 (.in0(S77), .in1({8{1'b0}}), .out(S93), .sel(RESET));
  Multiplexer #(.select(1), .width(1)) multiplexer_22 (.in0(S88), .in1(1'b0), .out(S99), .sel(RESET));

  // Other names for the same wires on the sheet: S0[7:0] = IR; S45 = S4[0]; S46 = S4[1]; S47 = S4[2]; S48 = S4[3];
  //   S6 = PHASE[0]; S8[1:0] = PHASE; S7 = PHASE[1]; S23[1:0] = {S22, S21}; S24[7:0] = ACC; S37 = S36[0];
  //   S38 = S36[1]; S39 = S36[2]; S40 = S36[3]; S41 = S36[4]; S42 = S36[5]; S43 = S36[6]; S44 = S36[7]; S58 = HALTED;
  //   S59 = ERROR; S61 = EN; S64 = RESET; S65[3:0] = PC; S76[7:0] = INSTR; S78 = Z; S82 = C; S89 = CLK
endmodule
