// Logisim project reg8.circ as structural Verilog: 1 circuit, main circuit REG8
module REG8 (
  input  [7:0] D,
  input  CLK,
  input  RESET,
  input  EN,
  output [7:0] Q
);

  wire [7:0] M1, M2;

  // NOT_Gate not_1 is placed but not wired
  Multiplexer #(.select(1), .width(8)) multiplexer_1 (.in0(Q), .in1(D), .out(M1), .sel(EN));
  Multiplexer #(.select(1), .width(8)) multiplexer_2 (.in0(M1), .in1({8{1'b0}}), .out(M2), .sel(RESET));
  Register #(.width(8)) register_1 (.D(M2), .en(1'b1), .clk(CLK), .Q(Q), .clr(1'b0));
endmodule
